# Fritzing sketch circuit (saved by Fritzing 0.9.3b)

parts:
  Part1 = Arduino Pro Mini (3.3V)
  MCU1 = Raspberry Pi Zero
  Part2 = Barometric Pressure Sensor - BMP180 Breakout (GY-68)
  PWM1 = PCA9685 16x12-bit PWM Breakout
  BAT1 = 18650 battery holder [package=battery-18650-kit]
  BAT2 = 18650 battery holder [package=battery-18650-kit]
  D1 = SOLAR-IXYS [package=solarbit-12x1]
  Part3 = TP4056 Charger
  Part4 = TP4056 Charger
  D2 = SOLAR-IXYS [package=solarbit-12x1]
  J1 = Basic Servo
  J2 = Basic Servo
  J3 = Basic Servo
  J4 = Basic Servo
  J5 = Basic Servo
  J6 = Basic Servo
  J7 = Basic Servo
  J8 = Basic Servo
  U2 = Voltage Regulator [package=to220-adj]
  Part5 = SRF05 Ultrasonic Rangefinder

nets:
  VCC: Part1.VCC, MCU1.pin_4, Part2.VCC, PWM1.no_name_yet#505, PWM1.no_name_yet#605, BAT1.+, Part3.IN+, Part3.BAT+, D2.C, U2.IN, Part5.VCC
  GND: Part1.GND, MCU1.pin_6, MCU1.pin_34, MCU1.pin_39, Part2.GND, PWM1.no_name_yet#501, PWM1.no_name_yet#601, PWM1.no_name_yet#701, PWM1.no_name_yet#1000, PWM1.no_name_yet#1001, PWM1.no_name_yet#1002, PWM1.no_name_yet#1003, PWM1.no_name_yet#1004, PWM1.no_name_yet#1005, PWM1.no_name_yet#1006, PWM1.no_name_yet#1007, BAT1.-, D1.A, Part3.IN-, Part3.BAT-, Part4.IN-, Part4.BAT-, D2.A, U2.OUT, Part5.GND
  N1: Part1.A4, MCU1.pin_3, Part2.SDA, PWM1.no_name_yet#504, PWM1.no_name_yet#604
  N2: Part1.A5, MCU1.pin_5, Part2.SCL, PWM1.no_name_yet#503, PWM1.no_name_yet#603
  N3: Part1.SCK, MCU1.pin_18
  N4: Part1.MISO, MCU1.pin_12
  N5: Part1.MOSI, MCU1.pin_16
  N6: Part1.D6, Part5.Trig
  N7: Part1.D5, Part5.Echo
  N8: Part1.RESET, MCU1.pin_32
  N9: PWM1.no_name_yet#0, J8.pulse
  N10: PWM1.no_name_yet#1, J1.pulse
  N11: PWM1.no_name_yet#2, J2.pulse
  N12: PWM1.no_name_yet#3, J3.pulse
  N13: PWM1.no_name_yet#4, J4.pulse
  N14: PWM1.no_name_yet#5, J5.pulse
  N15: PWM1.no_name_yet#6, J6.pulse
  N16: PWM1.no_name_yet#7, J7.pulse
  N17: PWM1.no_name_yet#100, PWM1.no_name_yet#101, PWM1.no_name_yet#102, PWM1.no_name_yet#103, PWM1.no_name_yet#104, PWM1.no_name_yet#105, PWM1.no_name_yet#106, PWM1.no_name_yet#107, PWM1.no_name_yet#706, BAT2.+, D1.C, Part4.IN+, Part4.BAT+

custom parts:
  18650 battery holder: 18650 Battery Holder
